# Fritzing sketch sketch_componenti (saved by Fritzing 0.9.3b)

parts:
  Componente2 = Arduino Motor Shield (Rev3)
  M1 = DC Motor
  VCC1 = 4 x AAA Battery Mount
  hc-sr1 = hc-sr04
  M2 = DC Motor
  J1 = Basic Servo
  J2 = Basic Servo
  Componente3 = Arduino Uno (Rev3)  # not connected

nets:
  N1: Componente2.D9/BreakeA, hc-sr1.Echo
  N2: Componente2.D10_PWM, hc-sr1.Trig
  N3: Componente2.D5_PWM, J2.pulse
  N4: Componente2.D6_PWM, J1.pulse
  N5: Componente2.B-, M1.pin_2
  N6: Componente2.B+, M1.pin_1
  N7: Componente2.A-, M2.pin_2
  N8: Componente2.A+, M2.pin_1
  N9: Componente2.VMOT, VCC1.+
  GND: Componente2.GND, VCC1.-, hc-sr1.GND
  VCC: Componente2.5V, hc-sr1.VCC, J2.vcc
